# Fritzing sketch weather_sensor_shield (saved by Fritzing 0.6.2b)
breadboards: 1

parts:
  Arduino1 = Arduino
  U1 = XBee
  D1 = Rectifier Diode [part_number=1N4001 package="300 mil [THT]"]
  D2 = Rectifier Diode [part_number=1N4001 package="300 mil [THT]"]
  R1 = Resistor [tolerance=±5% resistance=10k package=THT]
  R2 = Resistor [tolerance=±5% resistance=10k package=THT]
  D3 = Rectifier Diode [part_number=1N4001 package="300 mil [THT]"]

nets:
  GND: Arduino1.GND, U1.GND
  N1: Arduino1.D1TX, R2.Pin_0
  N2: Arduino1.D0RX, D1.anode
  3V3: Arduino1.3V3, U1.VCC, D2.cathode, D3.anode
  N3: Arduino1.+5V, R1.Pin_1
  N4: U1.pin2, D1.cathode, D2.anode, R1.Pin_0
  N5: U1.pin3, R2.Pin_1, D3.cathode
